# Fritzing sketch TrafficLightsSketch (saved by Fritzing 0.8.3b)
breadboards: 1

parts:
  Bauteil1 = Arduino Uno (Rev3)
  LED1 = LED - 5mm [color="Red (633nm)" package="5 mm [THT]"]
  LED3 = LED - 5mm [color="Green (570nm)" package="5 mm [THT]"]
  LED2 = smd LED [color="Yellow (595nm)" package="0603 [SMD]"]

nets:
  N1: Bauteil1.GND, LED1.cathode, LED3.cathode, LED2.cathode
  N2: Bauteil1.D8, LED3.anode
  N3: Bauteil1.D9_PWM, LED2.anode
  N4: Bauteil1.D10_PWM/SS, LED1.anode
